# Fritzing sketch PlantMonitor (saved by Fritzing 0.9.1b)
breadboards: 1

parts:
  Atmel_328 = Arduino Uno (Rev3)
  16x2 = LCD screen
  R2 = Photocell (LDR) [package=THT]
  R3 = Resistor [tolerance=±5% resistance=220 package=THT]
  R4 = Resistor [tolerance=±5% resistance=220 package=THT]
  C1 = Electrolytic Capacitor [capacitance=22µF package="100 mil [THT, electrolytic]"]
  U1 = mystery part, 4 pins [chip_label="M Sens"]
  R5 = Trimmer Potentiometer [maximum_resistance=10kΩ package=THT]
  R6 = Trimmer Potentiometer [maximum_resistance=10kΩ package=THT]
  R1 = Trimmer Potentiometer [maximum_resistance=10kΩ package=THT]
  IC1 = IC, DIP package, 8 pins [chip_label=LM158]
  LED1 = LED - 5mm [color="Red (633nm)" package="5 mm [THT]"]
  R7 = Resistor [tolerance=±5% resistance=220 package=THT]

nets:
  N1: Atmel_328.A0, U1.pin4
  N2: Atmel_328.A1, R2.pin_0, R3.Pin_1
  N3: Atmel_328.A2, R5.wiper
  N4: Atmel_328.A3, R6.wiper
  N5: Atmel_328.D9_PWM, R4.Pin_1
  N6: Atmel_328.D10_PWM/SS, LED1.anode
  GND: Atmel_328.GND, 16x2.VSS, 16x2.R/W, 16x2.LED-, R2.pin_1, C1.-, U1.pin2, R5.leg1, R6.leg1, R1.leg1, IC1.pin4, R7.Pin_1
  N7: Atmel_328.D2, 16x2.DB7
  N8: Atmel_328.D3_PWM, 16x2.DB6
  N9: Atmel_328.D4, 16x2.DB5
  N10: Atmel_328.D5_PWM, 16x2.DB4
  N11: Atmel_328.D6_PWM, 16x2.E
  N12: Atmel_328.D7, 16x2.RS
  5V: Atmel_328.5V, 16x2.VDD, R3.Pin_0, U1.pin1, R5.leg2, R6.leg2, R1.leg2
  N13: 16x2.V0, R1.wiper
  N14: 16x2.LED+, IC1.pin1, IC1.pin2
  N15: R4.Pin_0, C1.+, IC1.pin3
  9V: IC1.pin8
  N16: LED1.cathode, R7.Pin_0
